# Fritzing sketch mercurio (saved by Fritzing 0.7.11b)
breadboards: 1

parts:
  Arduino1 = Arduino
  LCD1 = LCD screen
  R2 = Rotary Potentiometer (Small)
  R3 = 10k Ω Resistor [package=THT]
  S1 = Round Pushbutton
  R1 = Rotary Potentiometer (Large) [maximum_resistance=100kΩ package=THT]

nets:
  N1: Arduino1.D12, LCD1.E
  N2: Arduino1.D11, LCD1.RS
  N3: Arduino1.D5, LCD1.DB7
  N4: Arduino1.D4, LCD1.DB6
  N5: Arduino1.D3, LCD1.DB5
  N6: Arduino1.D2, LCD1.DB4
  +5V: Arduino1.+5V, LCD1.VDD, LCD1.LED+, R2.leg2, S1.leg0, R1.leg2
  GND: Arduino1.GND, LCD1.VSS, LCD1.R/W, LCD1.LED-, R2.leg1, R3.Pin_1, R1.leg1
  N7: Arduino1.A0, R1.wiper
  N8: Arduino1.A1, R3.Pin_0, S1.leg1
  N9: LCD1.V0, R2.wiper
